// Logisim project cs25410_circuit.circ as structural Verilog: 1 circuit, main circuit main
module main (
  input  Reset,
  input  Direction
);

  wire and_1_out, and_2_out, and_3_out, and_4_out, and_5_out, and_6_out, and_7_out, and_8_out, and_9_out,
       and_10_out, and_11_out, clock_1_out, j_k_ff_1_q, j_k_ff_1_qn, j_k_ff_2_q, j_k_ff_2_qn, j_k_ff_3_q,
       j_k_ff_3_qn, j_k_ff_4_qn, not_1_out, not_2_out, not_3_out, not_4_out, or_1_out, or_2_out, or_3_out,
       or_4_out, or_5_out, or_6_out, or_7_out, or_8_out, or_9_out;

  Clock clock_1 (.out(clock_1_out));
  not not_1 (not_1_out, Direction);
  or or_1 (or_1_out, Direction, not_1_out);
  J_K_Flip_Flop j_k_ff_1 (
    .J(or_1_out), .clk(clock_1_out), .K(or_1_out), .Q(j_k_ff_1_q), .Qn(j_k_ff_1_qn), .preset(or_2_out));  // open: en, reset
  J_K_Flip_Flop j_k_ff_2 (
    .J(or_1_out), .clk(j_k_ff_1_q), .K(or_1_out), .Q(j_k_ff_2_q), .Qn(j_k_ff_2_qn), .preset(or_2_out));  // open: en, reset
  J_K_Flip_Flop j_k_ff_3 (
    .J(or_1_out), .clk(j_k_ff_2_q), .K(or_1_out), .Q(j_k_ff_3_q), .Qn(j_k_ff_3_qn), .preset(or_2_out));  // open: en, reset
  J_K_Flip_Flop j_k_ff_4 (
    .J(or_1_out), .clk(j_k_ff_3_q), .K(or_1_out), .Qn(j_k_ff_4_qn), .preset(or_2_out));  // open: Q, en, reset
  or or_2 (or_2_out, Reset, and_1_out);
  not not_2 (not_2_out, j_k_ff_1_qn);
  not not_3 (not_3_out, j_k_ff_2_qn);
  not not_4 (not_4_out, j_k_ff_3_qn);
  and and_1 (and_1_out, j_k_ff_2_qn, not_2_out, not_4_out, j_k_ff_4_qn);
  and and_2 (and_2_out, j_k_ff_1_qn, j_k_ff_2_qn);
  and and_3 (and_3_out, j_k_ff_3_qn, not_3_out);
  and and_4 (and_4_out, not_3_out, not_2_out);
  and and_5 (and_5_out, not_2_out, not_4_out);
  and and_6 (and_6_out, not_4_out, j_k_ff_2_qn);
  and and_7 (and_7_out, j_k_ff_2_qn, not_2_out);
  and and_8 (and_8_out, j_k_ff_3_qn, not_3_out, j_k_ff_1_qn);
  and and_9 (and_9_out, j_k_ff_3_qn, not_2_out);
  and and_10 (and_10_out, j_k_ff_3_qn, j_k_ff_1_qn);
  or or_3 (or_3_out, and_6_out, and_7_out, j_k_ff_4_qn, and_3_out);
  or or_4 (or_4_out, and_5_out, and_7_out);
  or or_5 (or_5_out, and_5_out, and_6_out, and_7_out, and_8_out, j_k_ff_4_qn);
  or or_6 (or_6_out, not_3_out, j_k_ff_1_qn, j_k_ff_3_qn);
  _7_Segment_Display u_7_segment_display_1 (
    .g(or_3_out), .f(or_8_out), .a(or_9_out), .b(or_7_out), .e(or_4_out), .d(or_5_out), .c(or_6_out));  // open: dp
  or or_7 (or_7_out, and_4_out, and_2_out, not_4_out);
  or or_8 (or_8_out, and_4_out, j_k_ff_4_qn, and_3_out, and_9_out);
  or or_9 (or_9_out, j_k_ff_4_qn, and_5_out, j_k_ff_2_qn, and_10_out);
  // AND_Gate and_11 has open pins: out=and_11_out
  // OR_Gate or_10 has open pins: in0=and_11_out, out=open
endmodule
